# Fritzing sketch spi_circuit (saved by Fritzing 0.9.3b)
breadboards: 1

parts:
  J1 = STM32 Nucleo boards
  IC2 = IC, DIP package, 8 pins [chip_label=MCP]
  R1 = TSR-3386UT Square Trimming Potentiometer [part_number=TSR-3386]

nets:
  N1: J1.D10_PWM/SS, IC2.pin1
  N2: J1.D11_PWM/MOSI, IC2.pin7
  N3: J1.D12/MISO, IC2.pin6
  N4: J1.D13/SCK, IC2.pin5
  N5: J1.3V3, IC2.pin8, R1.Leg2
  N6: J1.GND#1188, IC2.pin4, R1.Leg1
  N7: IC2.pin2, R1.wiper

custom parts:
  TSR-3386UT Square Trimming Potentiometer: Trimpot 10K with Knob
